# Fritzing sketch jemuran-otomatis-schematic (saved by Fritzing 0.9.3b)

parts:
  Part1 = Arduino Uno (Rev3)
  YL-83_-_Detection_Board1 = YL-83 Rain Sensor - Detection Board
  YL-83_-_Control_Board1 = YL-83 Rain Sensor - Control Board
  SERVO1 = Tower Pro SG90 servo [part_number=101246]

nets:
  N1: Part1.D8, YL-83_-_Control_Board1.DO
  N2: Part1.D9_PWM, SERVO1.Signal
  N3: Part1.D7, YL-83_-_Control_Board1.VCC
  5V: Part1.5V, SERVO1.+5V
  GND: Part1.GND, YL-83_-_Control_Board1.GND, SERVO1.GND
  N4: YL-83_-_Detection_Board1.POS, YL-83_-_Control_Board1.POS
  N5: YL-83_-_Detection_Board1.NEG, YL-83_-_Control_Board1.NEG

custom parts:
  YL-83 Rain Sensor - Detection Board: The YL-83 is a rain sensor that has more resistance when dry and less resistance when wet. The module runs at 5V.
  YL-83 Rain Sensor - Control Board: The YL-83 is a rain sensor that has more resistance when dry and less resistance when wet. The module runs at 5V.
  Tower Pro SG90 servo: Original file by John De Cristofaro http://www.adafruit.com/products/1449 Adafruit Feedback Servo (Small) Edited by: e-radionica.com 28/9/2015
